// Logisim project projey_uas.circ as structural Verilog: 1 circuit, main circuit main
module main (
);

  wire and_1_out, and_2_out, and_3_out, and_4_out, clock_1_out, d_ff_1_q, d_ff_2_q, not_1_out, not_2_out,
       xor_1_out;

  Clock clock_1 (.out(clock_1_out));
  xor xor_1 (xor_1_out, d_ff_1_q, d_ff_2_q);
  D_Flip_Flop d_ff_1 (.D(xor_1_out), .clk(clock_1_out), .Q(d_ff_1_q));  // open: Qn, preset, reset
  not not_1 (not_1_out, d_ff_1_q);
  D_Flip_Flop d_ff_2 (.D(not_2_out), .clk(clock_1_out), .Q(d_ff_2_q));  // open: Qn, preset, reset
  and and_1 (and_1_out, d_ff_2_q, not_1_out);
  not not_2 (not_2_out, d_ff_2_q);
  and and_2 (and_2_out, d_ff_2_q, d_ff_1_q);
  and and_3 (and_3_out, not_1_out, not_2_out);
  and and_4 (and_4_out, not_2_out, d_ff_1_q);
  LED led_1 (.in(d_ff_1_q));
  LED led_2 (.in(and_1_out));
  LED led_3 (.in(and_3_out));
  LED led_4 (.in(not_1_out));
  LED led_5 (.in(and_4_out));
  LED led_6 (.in(and_2_out));
endmodule
